# Fritzing sketch arduino-ac-ir-airlift (saved by Fritzing 0.9.4)
breadboards: 1

parts:
  IR1 = TSOP312.., 314.. [package=THT]
  LED1 = LED - 3mm [color="Infrared (940nm)" package="3 mm [THT]"]
  Part3 = Arduino Uno (Rev3) - ICSP
  Q1 = TRANSISTOR_NPN [package=to-92-ammo]
  Part2 = Adafruit Airlift Shield

nets:
  N1: IR1.GND, Q1.E, Part2.GND@2
  N2: IR1.Vs, LED1.anode, Part2.+5V
  N3: IR1.Data, Part2.D11
  N4: LED1.cathode, Q1.C
  N5: Part3.ICSP_MISO, Part2.MISO_ICSP
  N6: Part3.5V, Part2.5V_ICSP
  N7: Part3.ICSP_SCK, Part3.D13/SCK, Part2.SCK_ICSP
  N8: Part3.ICSP_MOSI, Part3.D11_PWM/MOSI, Part2.MOSI_ICSP
  N9: Part3.RESET, Part2.RESET_ICSP
  GND: Part3.GND, Part2.GND
  N10: Part3.D3_PWM, Q1.B, Part2.D3

custom parts:
  Adafruit Airlift Shield: Give your Arduino project a lift with the Adafruit AirLift Shield - a shield that lets you use the powerful ESP32 as a WiFi co-processor. You probably have your favorite Arduino-compatible (like the Metro M4 or the classic Metro 328) that comes with its own set of awesome peripherals and lots of libraries. But it doesn't have WiFi built in! So lets give that chip a best friend, the ESP32. This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
